// Logisim project 2 BIT HALF ADDER EX-26.circ as structural Verilog: 1 circuit, main circuit main
module main (
  input  A,
  input  B,
  output CARRY__A_B,
  output SUM__A_XOR_B
);

  wire NOR_2_out, NOR_3_out, NOR_out;

  nor NOR (NOR_out, A, B);
  nor NOR_2 (NOR_2_out, A, NOR_out);
  nor NOR_3 (NOR_3_out, NOR_out, B);
  nor NOR_4 (CARRY__A_B, NOR_2_out, NOR_3_out);
  nor NOR_5 (SUM__A_XOR_B, NOR_out, NOR_out);
endmodule
