// Logisim project 2 bit half adder.circ as structural Verilog: 1 circuit, main circuit main
module main (
  input  A,
  input  B,
  output CARRY__A_B,
  output SUM___A_XOR_B
);

  wire NOR_2_out, NOR_3_out, NOR_out;

  nor NOR (NOR_out, A, A);
  nor NOR_2 (NOR_2_out, A, B);
  nor NOR_3 (NOR_3_out, B, B);
  nor NOR_4 (CARRY__A_B, NOR_out, NOR_3_out);
  nor NOR_5 (SUM___A_XOR_B, CARRY__A_B, NOR_2_out);
endmodule
