// Logisim project 4 BIT CARRY LOOK ADDER EX-30.circ as structural Verilog: 1 circuit, main circuit main
module main (
  input  c_in,
  input  A,
  input  B,
  output SUM__A_XOR_B_XOR_Cin,
  output Cp___A_B,
  output Cg__A_B
);

  wire XOR_out;

  xor XOR (XOR_out, A, B);
  xor XOR_2 (SUM__A_XOR_B_XOR_Cin, c_in, XOR_out);
  or OR (Cp___A_B, B, A);
  and AND (Cg__A_B, B, A);
endmodule
