// Logisim project FULL ADDER CIRCUIT EX-16.circ as structural Verilog: 1 circuit, main circuit main
module main (
  input  A,
  input  B,
  input  C_in,
  output SUM___A_XOR_B__XOR_C,
  output CARRY__A_B__A_XOR_B
);

  wire AND_2_out, AND_out, XOR_out;

  xor XOR (XOR_out, A, B);
  and AND (AND_out, A, B);
  xor XOR_2 (SUM___A_XOR_B__XOR_C, XOR_out, C_in);
  and AND_2 (AND_2_out, XOR_out, C_in);
  or OR (CARRY__A_B__A_XOR_B, AND_2_out, AND_out);
endmodule
