// Logisim project FULL ADDER USING NOR GATE EX-29.circ as structural Verilog: 1 circuit, main circuit main
module main (
  input  A,
  input  B,
  input  C_in,
  output SUM___A_XOR_B,
  output CARRY__A_B
);

  wire NAND_2_out, NAND_3_out, NAND_4_out, NAND_5_out, NAND_6_out, NAND_7_out, NAND_out;

  nand NAND (NAND_out, A, B);
  nand NAND_2 (NAND_2_out, A, NAND_out);
  nand NAND_3 (NAND_3_out, NAND_out, B);
  nand NAND_4 (NAND_4_out, NAND_2_out, NAND_3_out);
  nand NAND_5 (NAND_5_out, NAND_4_out, C_in);
  nand NAND_6 (NAND_6_out, NAND_5_out, C_in);
  nand NAND_7 (NAND_7_out, NAND_4_out, NAND_5_out);
  nand NAND_8 (SUM___A_XOR_B, NAND_7_out, NAND_6_out);
  nand NAND_9 (CARRY__A_B, NAND_5_out, NAND_out);
endmodule
