// Logisim project FULL ADDER WITH NAND GATE EX-28.circ as structural Verilog: 1 circuit, main circuit main
module main (
  input  A,
  input  B,
  input  C_in,
  output SUM,
  output CARRY
);

  wire NAND_2_out, NAND_3_out, NAND_4_out, NAND_5_out, NAND_6_out, NAND_7_out, NAND_out;

  nand NAND (NAND_out, A, B);
  nand NAND_2 (NAND_2_out, A, NAND_out);
  nand NAND_3 (NAND_3_out, NAND_out, B);
  nand NAND_4 (NAND_4_out, NAND_2_out, NAND_3_out);
  nand NAND_5 (NAND_5_out, NAND_4_out, C_in);
  nand NAND_6 (NAND_6_out, NAND_4_out, NAND_5_out);
  nand NAND_7 (NAND_7_out, NAND_5_out, C_in);
  nand NAND_8 (SUM, NAND_6_out, NAND_7_out);
  nand NAND_9 (CARRY, NAND_5_out, NAND_out);
endmodule
