// Logisim project HALF ADDER WITH NAND GATE EX-17.circ as structural Verilog: 1 circuit, main circuit main
module main (
  input  in_1,
  input  in_2,
  output SUM__A_XOR_B,
  output CARRY__A_B
);

  wire NAND_2_out, NAND_3_out, NAND_out;

  nand NAND (NAND_out, in_1, in_2);
  nand NAND_2 (NAND_2_out, in_1, NAND_out);
  nand NAND_3 (NAND_3_out, NAND_out, in_2);
  nand NAND_4 (SUM__A_XOR_B, NAND_2_out, NAND_3_out);
  nand NAND_5 (CARRY__A_B, NAND_out, NAND_out);
endmodule
