// Logisim project HALF ADDER WITH XOR AND AND GATE EX-15.circ as structural Verilog: 1 circuit, main circuit main
module main (
  input  in_1,
  input  in_2,
  output SUM_A_XOR_B,
  output C__A_B
);

  xor ex_or (SUM_A_XOR_B, in_1, in_2);
  and \and  (C__A_B, in_1, in_2);
endmodule
